# Fritzing sketch Afik (saved by Fritzing 0.9.2b)
breadboards: 1

parts:
  U1 = 74HC595 SMD [package="SO16 [SMD]"]  # not connected
  DI1 = 7-Segment LED Display [package=THT]
  R1 = Resistor [tolerance=±5% resistance=220 package=THT]
  L1 = Inductor [package="400 mil [THT]"]

nets:
  N1: DI1.commAnode#2, L1.pin_0
  N2: DI1.commAnode#7, R1.Pin_1, L1.pin_1
