# Fritzing sketch Aryya (saved by Fritzing 0.9.2b)
breadboards: 1

parts:
  R1 = Photocell (LDR) [package=THT]
  L1 = Inductor [package="400 mil [THT]"]
  L2 = Inductor [package="400 mil [THT]"]
  L3 = Inductor [package="400 mil [THT]"]
  R2 = Resistor [tolerance=±5% resistance=220 package=THT]
  L4 = Inductor [package="0603 [SMD]"]
  L4_2 = Inductor [package="0603 [SMD]"]
  L4_3 = Inductor [package="400 mil [THT]"]
  L5 = Inductor [package="400 mil [THT]"]
  LED1 = LED - 5mm [color="Red (633nm)" package="5 mm [THT]"]  # not connected
  R3 = Resistor [tolerance=±5% resistance=220 package=THT]
  L6 = Inductor [package="400 mil [THT]"]
  R4 = Resistor [tolerance=±5% resistance=220 package=THT]
  S1 = Pushbutton [package="[THT]"]
  L7 = Inductor [package="400 mil [THT]"]
  L8 = Inductor [package="400 mil [THT]"]
  L9 = Inductor [package="400 mil [THT]"]
  L10 = Inductor [package="400 mil [THT]"]
  LED2 = LED - 5mm [color="Red (633nm)" package="5 mm [THT]"]
  Part1 = Arduino Uno (Rev3)

nets:
  N1: R1.pin_0, R2.Pin_1, Part1.A0
  N2: R1.pin_1, L3.pin_1
  N3: L1.pin_0, L1.pin_1, L3.pin_0, L6.pin_0, Part1.5V
  N4: L2.pin_0, L2.pin_1, L4.pin_0, L4_2.pin_0, L4_3.pin_0, L9.pin_0, Part1.GND
  N5: R2.Pin_0, L4.pin_1, L4_2.pin_1, L4_3.pin_1, L5.pin_1
  N6: R3.Pin_0, Part1.D11_PWM/MOSI
  N7: L6.pin_1, R4.Pin_0
  N8: R4.Pin_1, S1.Pin_1, S1.Pin_2, S1.Pin_3, S1.Pin_4, L7.pin_1, L8.pin_1, Part1.D2
  N9: L7.pin_0, L8.pin_0, L9.pin_1, L10.pin_0
  N10: L10.pin_1, LED2.cathode
  N11: LED2.anode, Part1.D6_PWM
