# Fritzing sketch Final (saved by Fritzing 0.9.2b)
breadboards: 3

parts:
  Part2 = Arduino Uno (Rev3)
  R5 = Photocell (LDR) [package=THT]
  L11 = Inductor [package="400 mil [THT]"]
  L12 = Inductor [package="400 mil [THT]"]
  L13 = Inductor [package="400 mil [THT]"]
  R6 = Resistor [tolerance=±5% resistance=220 package=THT]
  L14 = Inductor [package="400 mil [THT]"]
  L15 = Inductor [package="0603 [SMD]"]
  L16 = Inductor [package="0603 [SMD]"]
  L17 = Inductor [package="400 mil [THT]"]
  R7 = Resistor [tolerance=±5% resistance=220 package=THT]
  L18 = Inductor [package="400 mil [THT]"]
  R8 = Resistor [tolerance=±5% resistance=220 package=THT]
  L19 = Inductor [package="400 mil [THT]"]
  L20 = Inductor [package="400 mil [THT]"]
  L21 = Inductor [package="400 mil [THT]"]
  L22 = Inductor [package="400 mil [THT]"]
  LED4 = LED - 5mm [color="Red (633nm)" package="5 mm [THT]"]
  LED3 = LED - 5mm [color="Red (633nm)" package="5 mm [THT]"]
  S2 = Pushbutton [package="[THT]"]
  U2 = 74HC595 SMD [package="SO16 [SMD]"]
  DI2 = 7-Segment LED Display [package=THT]
  R9 = Resistor [tolerance=±5% resistance=220 package=THT]
  L23 = Inductor [package="400 mil [THT]"]
  Part3 = Arduino Uno (Rev3)
  M1 = DC Motor
  J1 = Piezo Speaker

nets:
  N1: Part2.A0, R5.pin_0, R6.Pin_1
  N2: Part2.D10_PWM/SS, J1.pin1
  N3: Part2.D13/SCK, R7.Pin_0
  N4: Part2.D2, R8.Pin_1, L19.pin_1, L20.pin_1, S2.Pin_1, S2.Pin_2, S2.Pin_3, S2.Pin_4
  N5: Part2.D5_PWM, LED4.anode
  3V3: Part2.3V3, U2.Q1, U2.Q2, U2.Q0, U2.VCC
  GND: Part2.GND, U2.GND, R9.Pin_0, J1.pin2
  N6: R5.pin_1, L13.pin_1
  N7: L11.pin_0, L11.pin_1, L13.pin_0, L18.pin_0
  N8: L12.pin_0, L12.pin_1, L14.pin_0, L15.pin_0, L16.pin_0, L21.pin_0
  N9: R6.Pin_0, L14.pin_1, L15.pin_1, L16.pin_1, L17.pin_1
  N10: L17.pin_0, LED3.cathode
  N11: R7.Pin_1, LED3.anode
  N12: L18.pin_1, R8.Pin_0
  N13: L19.pin_0, L20.pin_0, L21.pin_1, L22.pin_0
  N14: L22.pin_1, LED4.cathode
  N15: U2.Q4, DI2.cathodeG
  N16: U2.Q5, DI2.cathodeA
  N17: U2.Q6, DI2.cathodeF
  N18: U2.OE, DI2.cathodeB
  N19: DI2.commAnode#2, L23.pin_0
  N20: DI2.commAnode#7, R9.Pin_1, L23.pin_1
  N21: Part3.D3_PWM, Part3.D4, Part3.D5_PWM, Part3.D6_PWM, M1.pin_2
  N22: Part3.GND, M1.pin_1
